// Logisim project Substraction.circ as structural Verilog
module Substract (
  input  A,
  input  B,
  input  Bin,
  output D,
  output Bo
);

  wire and_1_out, and_2_out, and_3_out, and_4_out, and_5_out, and_6_out, and_7_out, not_1_out, not_2_out,
       not_3_out, not_4_out, not_5_out, not_6_out, not_7_out, not_8_out;

  not not_1 (not_1_out, A);
  not not_2 (not_2_out, B);
  not not_3 (not_3_out, A);
  not not_4 (not_4_out, Bin);
  not not_5 (not_5_out, B);
  not not_6 (not_6_out, Bin);
  not not_7 (not_7_out, A);
  not not_8 (not_8_out, A);
  and and_1 (and_1_out, not_1_out, not_2_out, Bin);
  and and_2 (and_2_out, not_3_out, B, not_4_out);
  and and_3 (and_3_out, A, not_5_out, not_6_out);
  and and_4 (and_4_out, A, B, Bin);
  and and_5 (and_5_out, not_7_out, Bin);
  and and_6 (and_6_out, not_8_out, B);
  and and_7 (and_7_out, B, Bin);
  or or_1 (D, and_1_out, and_2_out, and_3_out, and_4_out);
  or or_2 (Bo, and_5_out, and_6_out, and_7_out);
endmodule
