// Logisim project Tarea_2.circ as structural Verilog: 3 circuits, main circuit main
module main (
  input  [3:0] in_1,
  input  in_2,
  input  in_3,
  input  in_4,
  input  in_5,
  input  in_6,
  input  in_7,
  output out_8,
  output out_9,
  output out_10
);

  wire carga_bot_1_carga;

  Carga_Bot carga_bot_1 (
    .\Primer_Dígito (in_1[0]), .\Seguno_Dígito (in_1[1]), .\Tercer_Dígito (in_1[2]),
    .\Cuarto_Dígito (in_1[3]), .Carga(carga_bot_1_carga));
  Circuito_Bot circuito_bot_1 (
    .Bateria(carga_bot_1_carga), .Enemigo_Izq(in_2), .Enemigo_Frent(in_3), .Enemigo_Der(in_4),
    .Carga_Izq(in_5), .Carga_Frent(in_6), .Carga_Der(in_7), .L(out_8), .F(out_9), .R(out_10));
endmodule

module Circuito_Bot (
  input  Bateria,
  input  Enemigo_Izq,
  input  Enemigo_Frent,
  input  Enemigo_Der,
  input  Carga_Izq,
  input  Carga_Frent,
  input  Carga_Der,
  output L,
  output F,
  output R
);

  wire and_1_out, and_2_out, and_3_out, and_4_out, and_5_out, and_6_out, and_7_out, and_8_out, and_9_out,
       and_10_out, and_11_out, and_12_out, and_13_out, and_14_out, and_15_out, and_16_out, and_17_out,
       and_18_out, not_1_out, not_2_out, not_3_out, not_4_out, not_5_out, not_6_out, not_7_out, not_8_out,
       not_9_out, not_10_out, not_11_out, not_12_out, not_13_out, not_14_out, not_15_out, not_16_out,
       not_17_out, not_18_out, not_19_out, not_20_out, not_21_out, not_22_out, not_23_out, not_24_out,
       not_25_out, not_26_out, not_27_out, not_28_out, not_29_out, not_30_out, not_31_out, not_32_out,
       not_33_out, not_34_out, not_35_out, not_36_out, not_37_out, not_38_out, not_39_out, not_40_out,
       not_41_out, not_42_out, not_43_out, not_44_out, not_45_out, not_46_out, not_47_out, not_48_out,
       not_49_out, not_50_out, not_51_out, not_52_out, not_53_out, not_54_out, not_55_out, not_56_out,
       not_57_out, not_58_out, not_59_out, not_60_out, not_61_out, not_62_out, not_63_out, not_64_out,
       not_65_out, not_66_out, not_67_out, not_68_out, not_69_out, not_70_out, not_71_out;

  not not_1 (not_1_out, Bateria);
  not not_2 (not_2_out, Enemigo_Izq);
  not not_3 (not_3_out, Enemigo_Frent);
  not not_4 (not_4_out, Carga_Frent);
  not not_5 (not_5_out, Carga_Der);
  not not_6 (not_6_out, Bateria);
  not not_7 (not_7_out, Enemigo_Izq);
  not not_8 (not_8_out, Enemigo_Der);
  not not_9 (not_9_out, Carga_Frent);
  not not_10 (not_10_out, Carga_Der);
  not not_11 (not_11_out, Enemigo_Izq);
  not not_12 (not_12_out, Carga_Izq);
  not not_13 (not_13_out, Carga_Frent);
  not not_14 (not_14_out, Carga_Der);
  not not_15 (not_15_out, Enemigo_Izq);
  not not_16 (not_16_out, Enemigo_Frent);
  not not_17 (not_17_out, Carga_Izq);
  not not_18 (not_18_out, Enemigo_Izq);
  not not_19 (not_19_out, Enemigo_Der);
  not not_20 (not_20_out, Carga_Izq);
  not not_21 (not_21_out, Carga_Frent);
  not not_22 (not_22_out, Bateria);
  not not_23 (not_23_out, Enemigo_Frent);
  not not_24 (not_24_out, Carga_Izq);
  not not_25 (not_25_out, Carga_Der);
  not not_26 (not_26_out, Enemigo_Frent);
  not not_27 (not_27_out, Carga_Izq);
  not not_28 (not_28_out, Carga_Frent);
  not not_29 (not_29_out, Carga_Der);
  not not_30 (not_30_out, Bateria);
  not not_31 (not_31_out, Enemigo_Izq);
  not not_32 (not_32_out, Enemigo_Frent);
  not not_33 (not_33_out, Enemigo_Der);
  not not_34 (not_34_out, Bateria);
  not not_35 (not_35_out, Enemigo_Izq);
  not not_36 (not_36_out, Enemigo_Frent);
  not not_37 (not_37_out, Carga_Der);
  not not_38 (not_38_out, Bateria);
  not not_39 (not_39_out, Enemigo_Frent);
  not not_40 (not_40_out, Enemigo_Der);
  not not_41 (not_41_out, Carga_Izq);
  not not_42 (not_42_out, Enemigo_Izq);
  not not_43 (not_43_out, Enemigo_Frent);
  not not_44 (not_44_out, Carga_Frent);
  not not_45 (not_45_out, Enemigo_Frent);
  not not_46 (not_46_out, Enemigo_Der);
  not not_47 (not_47_out, Carga_Izq);
  not not_48 (not_48_out, Carga_Frent);
  not not_49 (not_49_out, Bateria);
  not not_50 (not_50_out, Enemigo_Izq);
  not not_51 (not_51_out, Enemigo_Der);
  not not_52 (not_52_out, Carga_Frent);
  not not_53 (not_53_out, Bateria);
  not not_54 (not_54_out, Enemigo_Der);
  not not_55 (not_55_out, Carga_Izq);
  not not_56 (not_56_out, Carga_Frent);
  not not_57 (not_57_out, Enemigo_Der);
  not not_58 (not_58_out, Carga_Izq);
  not not_59 (not_59_out, Carga_Frent);
  not not_60 (not_60_out, Carga_Der);
  not not_61 (not_61_out, Enemigo_Izq);
  not not_62 (not_62_out, Enemigo_Frent);
  not not_63 (not_63_out, Enemigo_Der);
  not not_64 (not_64_out, Carga_Der);
  not not_65 (not_65_out, Enemigo_Izq);
  not not_66 (not_66_out, Enemigo_Der);
  not not_67 (not_67_out, Carga_Frent);
  not not_68 (not_68_out, Enemigo_Frent);
  not not_69 (not_69_out, Enemigo_Der);
  not not_70 (not_70_out, Carga_Izq);
  not not_71 (not_71_out, Carga_Der);
  and and_1 (and_1_out, not_1_out, not_2_out, not_3_out, Carga_Izq, not_4_out, not_5_out);
  and and_2 (and_2_out, not_6_out, not_7_out, not_8_out, Carga_Izq, not_9_out, not_10_out);
  and and_3 (and_3_out, not_11_out, Enemigo_Frent, Enemigo_Der, not_12_out, not_13_out, not_14_out);
  and and_4 (and_4_out, Bateria, not_15_out, not_16_out, not_17_out, Carga_Frent);
  and and_5 (and_5_out, Bateria, not_18_out, Enemigo_Frent, not_19_out, not_20_out, not_21_out);
  and and_6 (and_6_out, not_22_out, not_23_out, not_24_out, not_25_out);
  and and_7 (and_7_out, not_26_out, not_27_out, not_28_out, not_29_out);
  and and_8 (and_8_out, not_30_out, not_31_out, not_32_out, not_33_out, Carga_Frent);
  and and_9 (and_9_out, not_34_out, not_35_out, not_36_out, Carga_Frent, not_37_out);
  and and_10 (and_10_out, not_38_out, not_39_out, not_40_out, not_41_out, Carga_Frent);
  and and_11 (and_11_out, Bateria, not_42_out, not_43_out, not_44_out);
  and and_12 (and_12_out, Bateria, not_45_out, not_46_out, not_47_out, not_48_out);
  and and_13 (and_13_out, not_49_out, not_50_out, not_51_out, not_52_out, Carga_Der);
  and and_14 (and_14_out, not_53_out, not_54_out, not_55_out, not_56_out, Carga_Der);
  and and_15 (and_15_out, Enemigo_Izq, Enemigo_Frent, not_57_out, not_58_out, not_59_out, not_60_out);
  and and_16 (and_16_out, Bateria, not_61_out, not_62_out, not_63_out, Carga_Izq, Carga_Frent, not_64_out);
  and and_17 (and_17_out, Bateria, not_65_out, Enemigo_Frent, not_66_out, Carga_Izq, not_67_out);
  and and_18 (and_18_out, Bateria, Enemigo_Izq, not_68_out, not_69_out, not_70_out, Carga_Frent, not_71_out);
  or or_1 (F, and_6_out, and_7_out, and_8_out, and_9_out, and_10_out, and_11_out, and_12_out);
  or or_2 (L, and_1_out, and_2_out, and_3_out, and_4_out, and_5_out);
  or or_3 (R, and_13_out, and_14_out, and_15_out, and_16_out, and_17_out, and_18_out);
endmodule

module Carga_Bot (
  input  \Primer_Dígito ,
  input  \Seguno_Dígito ,
  input  \Tercer_Dígito ,
  input  \Cuarto_Dígito ,
  output Carga
);

  or or_1 (Carga, \Tercer_Dígito , \Cuarto_Dígito );
endmodule
