// Logisim project Tarea_2_FINAL.circ as structural Verilog: 10 circuits, main circuit main
module main (
  input  Bit,
  input  Reset,
  input  in_3,
  input  in_4,
  input  in_5,
  input  in_6,
  input  in_7,
  input  in_8,
  output [3:0] out_9,
  output out_10,
  output out_11,
  output out_12
);

  wire carga_bot_1_carga, CLK_out;

  Clock CLK (.out(CLK_out));
  Contador contador_1 (
    .Bit(Bit), .Reset(Reset), .CLK(CLK_out), .O0(out_9[0]), .O1(out_9[1]), .O2(out_9[2]), .O3(out_9[3]));
  Carga_Bot carga_bot_1 (.A(out_9[0]), .B(out_9[1]), .C(out_9[2]), .D(out_9[3]), .Carga(carga_bot_1_carga));
  Circuito_Bot circuito_bot_1 (
    .Bateria(carga_bot_1_carga), .El(in_3), .Ef(in_4), .Er(in_5), .Cl(in_6), .Cf(in_7), .Cr(in_8),
    .L(out_10), .F(out_11), .R(out_12));
endmodule

module Circuito_Bot (
  input  Bateria,
  input  El,
  input  Ef,
  input  Er,
  input  Cl,
  input  Cf,
  input  Cr,
  output L,
  output F,
  output R
);

  wire and_1_out, and_2_out, and_3_out, and_4_out, and_5_out, and_6_out, and_7_out, and_8_out, and_9_out,
       and_10_out, and_11_out, and_12_out, and_13_out, and_14_out, and_15_out, and_16_out, and_17_out,
       and_18_out, and_19_out, and_20_out, and_21_out, and_22_out, not_1_out, not_2_out, not_3_out,
       not_4_out, not_5_out, not_6_out, not_7_out, not_8_out, not_9_out, not_10_out, not_11_out, not_12_out,
       not_13_out, not_14_out, not_15_out, not_16_out, not_17_out, not_18_out, not_19_out, not_20_out,
       not_21_out, not_22_out, not_23_out, not_24_out, not_25_out, not_26_out, not_27_out, not_28_out,
       not_29_out, not_30_out, not_31_out, not_32_out, not_33_out, not_34_out, not_35_out, not_36_out,
       not_37_out, not_38_out, not_39_out, not_40_out, not_41_out, not_42_out, not_43_out, not_44_out,
       not_45_out, not_46_out, not_47_out, not_48_out, not_49_out, not_50_out, not_51_out, not_52_out,
       not_53_out;

  not not_1 (not_1_out, Bateria);
  not not_2 (not_2_out, El);
  not not_3 (not_3_out, Cf);
  not not_4 (not_4_out, Cr);
  not not_5 (not_5_out, Bateria);
  not not_6 (not_6_out, El);
  not not_7 (not_7_out, Cf);
  not not_8 (not_8_out, Bateria);
  not not_9 (not_9_out, El);
  not not_10 (not_10_out, Cr);
  not not_11 (not_11_out, El);
  not not_12 (not_12_out, Cf);
  not not_13 (not_13_out, Cr);
  not not_14 (not_14_out, El);
  not not_15 (not_15_out, El);
  not not_16 (not_16_out, Cl);
  not not_17 (not_17_out, Ef);
  not not_18 (not_18_out, Er);
  not not_19 (not_19_out, Cl);
  not not_20 (not_20_out, El);
  not not_21 (not_21_out, Cl);
  not not_22 (not_22_out, El);
  not not_23 (not_23_out, Ef);
  not not_24 (not_24_out, Er);
  not not_25 (not_25_out, Cl);
  not not_26 (not_26_out, Cf);
  not not_27 (not_27_out, Cr);
  not not_28 (not_28_out, Ef);
  not not_29 (not_29_out, Ef);
  not not_30 (not_30_out, Bateria);
  not not_31 (not_31_out, Er);
  not not_32 (not_32_out, Cf);
  not not_33 (not_33_out, Bateria);
  not not_34 (not_34_out, Er);
  not not_35 (not_35_out, Er);
  not not_36 (not_36_out, Ef);
  not not_37 (not_37_out, Er);
  not not_38 (not_38_out, Cr);
  not not_39 (not_39_out, El);
  not not_40 (not_40_out, Cr);
  not not_41 (not_41_out, El);
  not not_42 (not_42_out, Er);
  not not_43 (not_43_out, Cf);
  not not_44 (not_44_out, Ef);
  not not_45 (not_45_out, Er);
  not not_46 (not_46_out, Cr);
  not not_47 (not_47_out, Er);
  not not_48 (not_48_out, Cl);
  not not_49 (not_49_out, Cf);
  and and_1 (and_1_out, not_1_out, not_2_out, Cl, not_3_out, not_4_out);
  and and_2 (and_2_out, not_5_out, not_6_out, Er, Cl, not_7_out);
  and and_3 (and_3_out, not_8_out, not_9_out, Ef, Cl, not_10_out);
  and and_4 (and_4_out, not_11_out, Ef, Er, not_12_out, not_13_out);
  and and_5 (and_5_out, not_14_out, Ef, Er, Cl);
  and and_6 (and_6_out, Bateria, not_15_out, not_16_out, Cf);
  and and_7 (and_7_out, Bateria, not_17_out, not_18_out, not_19_out, Cf, Cr);
  and and_8 (and_8_out, Bateria, not_20_out, Ef, not_21_out);
  and and_9 (and_9_out, Bateria, not_22_out, Ef, Cf);
  not not_50 (not_50_out, Bateria);
  and and_10 (and_10_out, not_50_out, not_51_out, Cf);
  not not_51 (not_51_out, Ef);
  and and_11 (and_11_out, El, not_23_out, not_24_out, not_25_out, not_26_out, not_27_out);
  and and_12 (and_12_out, Bateria, not_52_out, not_53_out);
  not not_52 (not_52_out, Ef);
  not not_53 (not_53_out, Cf);
  and and_13 (and_13_out, Bateria, not_28_out, Cl, Cr);
  and and_14 (and_14_out, Bateria, El, not_29_out, Er);
  and and_15 (and_15_out, not_30_out, not_31_out, not_32_out, Cr);
  and and_16 (and_16_out, not_33_out, Ef, not_34_out, Cr);
  and and_17 (and_17_out, El, Ef, not_35_out, Cr);
  and and_18 (and_18_out, Bateria, not_36_out, not_37_out, Cl, Cf, not_38_out);
  and and_19 (and_19_out, Bateria, not_39_out, Er, Cl, Cf, not_40_out);
  and and_20 (and_20_out, Bateria, not_41_out, Ef, not_42_out, Cl, not_43_out);
  and and_21 (and_21_out, Bateria, El, not_44_out, not_45_out, Cf, not_46_out);
  and and_22 (and_22_out, Bateria, El, Ef, not_47_out, not_48_out, not_49_out);
  or or_1 (F, and_10_out, and_11_out, and_12_out, and_13_out, and_14_out);
  or or_2 (L, and_1_out, and_2_out, and_3_out, and_4_out, and_5_out, and_6_out, and_7_out, and_8_out, and_9_out);
  or or_3 (R, and_15_out, and_16_out, and_17_out, and_18_out, and_19_out, and_20_out, and_21_out, and_22_out);
endmodule

module Carga_Bot (
  input  A,
  input  B,
  input  C,
  input  D,
  output Carga
);

  or or_1 (Carga, C, D);
endmodule

module _16_a_0 (
  input  I3,
  input  I2,
  input  I1,
  input  I0,
  output O3,
  output O2,
  output O1,
  output O0
);

  wire and_1_out, and_2_out, and_3_out, and_4_out, and_5_out, and_6_out, and_7_out, and_8_out, and_9_out,
       and_10_out, and_11_out, and_12_out, not_1_out, not_2_out, not_3_out, not_4_out, not_5_out, not_6_out,
       not_7_out, not_8_out, not_9_out, not_10_out;

  and and_1 (and_1_out, I3, I0);
  and and_2 (and_2_out, I3, I1);
  and and_3 (and_3_out, I3, I2);
  not not_1 (not_1_out, I2);
  not not_2 (not_2_out, I1);
  not not_3 (not_3_out, I0);
  and and_4 (and_4_out, I1, I0);
  not not_4 (not_4_out, I1);
  and and_5 (and_5_out, I2, not_4_out, not_5_out);
  not not_5 (not_5_out, I0);
  and and_6 (and_6_out, I3, not_6_out, not_7_out);
  not not_6 (not_6_out, I1);
  not not_7 (not_7_out, I0);
  and and_7 (and_7_out, I1, not_8_out);
  not not_8 (not_8_out, I0);
  and and_8 (and_8_out, I2, not_9_out);
  not not_9 (not_9_out, I0);
  and and_9 (and_9_out, I3, not_10_out);
  not not_10 (not_10_out, I0);
  or or_1 (O3, and_1_out, and_2_out, and_3_out);
  and and_10 (and_10_out, I2, I0);
  or or_2 (O2, and_10_out, and_11_out, and_12_out);
  and and_11 (and_11_out, I2, I1);
  and and_12 (and_12_out, I3, not_1_out, not_2_out, not_3_out);
  or or_3 (O1, and_4_out, and_5_out, and_6_out);
  or or_4 (O0, and_7_out, and_8_out, and_9_out);
endmodule

module SR_Latch (
  input  R,
  input  S,
  output Q,
  output Q_prime
);

  nor nor_1 (Q, R, Q_prime);
  nor nor_2 (Q_prime, Q, S);
endmodule

module D_Latch (
  input  CLK,
  input  D,
  output out_3,
  output out_4
);

  wire and_1_out, and_2_out, not_1_out;

  not not_1 (not_1_out, D);
  and and_1 (and_1_out, CLK, not_1_out);
  and and_2 (and_2_out, CLK, D);
  SR_Latch sr_latch_1 (.R(and_1_out), .S(and_2_out), .Q(out_3), .Q_prime(out_4));
endmodule

module D_Flip_Flop (
  input  Clock,
  input  Bit,
  output Q,
  output Q_prime
);

  wire d_latch_2_out_3, not_1_out;

  not not_1 (not_1_out, Clock);
  D_Latch d_latch_1 (.CLK(Clock), .D(d_latch_2_out_3), .out_3(Q), .out_4(Q_prime));
  D_Latch d_latch_2 (.CLK(not_1_out), .D(Bit), .out_3(d_latch_2_out_3));  // open: out_4
endmodule

module _0_a_16 (
  input  I3,
  input  I2,
  input  I1,
  input  I0,
  output O3,
  output O2,
  output O1,
  output O0
);

  wire and_1_out, and_2_out, and_3_out, and_4_out, and_5_out, and_6_out, and_7_out, and_8_out, and_9_out,
       not_1_out, not_2_out, not_3_out, not_4_out, not_5_out, not_6_out;

  and and_1 (and_1_out, I2, I1, I0);
  not not_1 (not_1_out, I2);
  and and_2 (and_2_out, not_1_out, I1, I0);
  and and_3 (and_3_out, I2, not_2_out);
  not not_2 (not_2_out, I1);
  and and_4 (and_4_out, I2, not_3_out);
  not not_3 (not_3_out, I0);
  and and_5 (and_5_out, I3, I2);
  not not_4 (not_4_out, I1);
  and and_6 (and_6_out, not_4_out, I0);
  and and_7 (and_7_out, I1, not_5_out);
  not not_5 (not_5_out, I0);
  and and_8 (and_8_out, I3, I2, I1);
  not not_6 (not_6_out, I0);
  and and_9 (and_9_out, I3, I2, I1);
  or or_1 (O3, and_1_out, I3);
  or or_2 (O2, and_2_out, and_3_out, and_4_out, and_5_out);
  or or_3 (O1, and_6_out, and_7_out, and_8_out);
  or or_4 (O0, not_6_out, and_9_out);
endmodule

module Delay (
  input  in_1,
  output out_2
);

  wire clock_1_out, not_1_out;

  Clock #(.highDuration(2), .lowDuration(2)) clock_1 (.out(clock_1_out));
  Multiplexer multiplexer_1 (.in0(in_1), .in1(1'b0), .out(out_2), .sel(clock_1_out), .en(not_1_out));
  not not_1 (not_1_out, clock_1_out);
endmodule

module Contador (
  input  Bit,
  input  Reset,
  input  CLK,
  output O0,
  output O1,
  output O2,
  output O3
);

  wire and_1_out, and_2_out, and_3_out, and_4_out, and_5_out, and_6_out, and_7_out, and_8_out,
       d_flip_flop_1_q, d_flip_flop_1_q_prime, d_flip_flop_2_q, d_flip_flop_2_q_prime, d_flip_flop_3_q,
       d_flip_flop_3_q_prime, d_flip_flop_4_q, d_flip_flop_4_q_prime, or_1_out, or_2_out, or_3_out, or_4_out,
       or_5_out, xor_1_out;

  and and_1 (and_1_out, d_flip_flop_3_q, d_flip_flop_1_q_prime);
  and and_2 (and_2_out, d_flip_flop_3_q, d_flip_flop_2_q_prime);
  and and_3 (and_3_out, d_flip_flop_3_q_prime, d_flip_flop_2_q, d_flip_flop_1_q);
  and and_4 (and_4_out, d_flip_flop_4_q, d_flip_flop_2_q_prime);
  and and_5 (and_5_out, d_flip_flop_4_q, d_flip_flop_1_q_prime);
  and and_6 (and_6_out, d_flip_flop_4_q, d_flip_flop_3_q_prime);
  and and_7 (and_7_out, d_flip_flop_4_q_prime, d_flip_flop_3_q, d_flip_flop_2_q, d_flip_flop_1_q);
  xor xor_1 (xor_1_out, d_flip_flop_1_q, d_flip_flop_2_q);
  or or_1 (or_1_out, and_1_out, and_2_out, and_3_out);
  or or_2 (or_2_out, and_4_out, and_5_out, and_6_out, and_7_out);
  and and_8 (and_8_out, d_flip_flop_1_q_prime, Bit);
  or or_3 (or_3_out, xor_1_out, Reset);
  or or_4 (or_4_out, or_1_out, Reset);
  or or_5 (or_5_out, or_2_out, Reset);
  D_Flip_Flop d_flip_flop_1 (.Clock(CLK), .Bit(and_8_out), .Q(d_flip_flop_1_q), .Q_prime(d_flip_flop_1_q_prime));
  D_Flip_Flop d_flip_flop_2 (.Clock(CLK), .Bit(or_3_out), .Q(d_flip_flop_2_q), .Q_prime(d_flip_flop_2_q_prime));
  D_Flip_Flop d_flip_flop_3 (.Clock(CLK), .Bit(or_4_out), .Q(d_flip_flop_3_q), .Q_prime(d_flip_flop_3_q_prime));
  D_Flip_Flop d_flip_flop_4 (.Clock(CLK), .Bit(or_5_out), .Q(d_flip_flop_4_q), .Q_prime(d_flip_flop_4_q_prime));
  not not_1 (O0, d_flip_flop_1_q);
  not not_2 (O1, d_flip_flop_2_q);
  not not_3 (O2, d_flip_flop_3_q);
  not not_4 (O3, d_flip_flop_4_q);
endmodule
